// Logisim project Pong_LED_Matrix.circ as structural Verilog: 22 circuits, main circuit main
module main (
  input  Multiplayer
);

  wire and_1_out, and_2_out, and_3_out, and_4_out, asciii_to_cmd_1_p1_down, asciii_to_cmd_1_p1_up,
       asciii_to_cmd_1_p2_down, asciii_to_cmd_1_p2_up, asciii_to_cmd_1_reset, clock_1_out,
       collisioncheck_1_collision, collisioncheck_1_corner, collisioncheck_2_collision,
       collisioncheck_2_corner, comparator_1_eq, comparator_2_eq, counters_1_logictick, or_1_out, or_2_out,
       startplayer_1_p2_next, startplayer_1_startdown, startplayer_1_startup;
  wire [3:0] ballpos_1_posx, ballpos_1_posxnext, counters_1_activex, multiplexer_1_out;
  wire [6:0] keyboard_1_data;
  wire [15:0] ballpos_1_draw, ballpos_1_posy, ballpos_1_posynext, Draw_out, playerpos_1_draw,
       playerpos_1_posy, playerpos_2_draw, playerpos_2_posy, vram16_1_out_4, vram16_1_out_5, vram16_1_out_6,
       vram16_1_out_7, vram16_1_out_8, vram16_1_out_9, vram16_1_out_10, vram16_1_out_11, vram16_1_out_12,
       vram16_1_out_13, vram16_1_out_14, vram16_1_out_15, vram16_1_out_16, vram16_1_out_17, vram16_1_out_18,
       vram16_1_out_19;

  Keyboard keyboard_1 (.clk(clock_1_out), .data(keyboard_1_data));  // open: re, clr, avail
  Clock clock_1 (.out(clock_1_out));
  VRAM16 vram16_1 (
    .Addr(counters_1_activex), .Wert(Draw_out), .Clk(clock_1_out), .out_4(vram16_1_out_4),
    .out_5(vram16_1_out_5), .out_6(vram16_1_out_6), .out_7(vram16_1_out_7), .out_8(vram16_1_out_8),
    .out_9(vram16_1_out_9), .out_10(vram16_1_out_10), .out_11(vram16_1_out_11), .out_12(vram16_1_out_12),
    .out_13(vram16_1_out_13), .out_14(vram16_1_out_14), .out_15(vram16_1_out_15), .out_16(vram16_1_out_16),
    .out_17(vram16_1_out_17), .out_18(vram16_1_out_18), .out_19(vram16_1_out_19));
  Counters counters_1 (.Clock(clock_1_out), .LogicTick(counters_1_logictick), .ActiveX(counters_1_activex));
  ASCIII_to_Cmd asciii_to_cmd_1 (
    .in_1(keyboard_1_data), .Reset(asciii_to_cmd_1_reset), .P1_Up(asciii_to_cmd_1_p1_up),
    .P1_Down(asciii_to_cmd_1_p1_down), .P2_Up(asciii_to_cmd_1_p2_up), .P2_Down(asciii_to_cmd_1_p2_down));
  DotMatrix #(.matrixcols(16), .matrixrows(16)) dotmatrix_1 (
    .col0(vram16_1_out_4), .col1(vram16_1_out_5), .col2(vram16_1_out_6), .col3(vram16_1_out_7),
    .col4(vram16_1_out_8), .col5(vram16_1_out_9), .col6(vram16_1_out_10), .col7(vram16_1_out_11),
    .col8(vram16_1_out_12), .col9(vram16_1_out_13), .col10(vram16_1_out_14), .col11(vram16_1_out_15),
    .col12(vram16_1_out_16), .col13(vram16_1_out_17), .col14(vram16_1_out_18), .col15(vram16_1_out_19));
  LED Player_A_Won (.in(and_1_out));
  LED Player_B_Won (.in(comparator_1_eq));
  Multiplexer #(.width(4)) multiplexer_1 (
    .in0(4'b0000), .in1(counters_1_activex), .out(multiplexer_1_out), .sel(Multiplayer));
  PlayerPos playerpos_1 (
    .ActiveX(counters_1_activex), .PosX(4'b0001), .moveUp(asciii_to_cmd_1_p1_up),
    .moveDown(asciii_to_cmd_1_p1_down), .Reset(asciii_to_cmd_1_reset), .Clock(clock_1_out),
    .Draw(playerpos_1_draw), .PosY(playerpos_1_posy));
  PlayerPos playerpos_2 (
    .ActiveX(multiplexer_1_out), .PosX(4'b1110), .moveUp(asciii_to_cmd_1_p2_up),
    .moveDown(asciii_to_cmd_1_p2_down), .Reset(asciii_to_cmd_1_reset), .Clock(clock_1_out),
    .Draw(playerpos_2_draw), .PosY(playerpos_2_posy));
  StartPlayer startplayer_1 (
    .P1_Up(asciii_to_cmd_1_p1_up), .P1_Down(asciii_to_cmd_1_p1_down), .P2_Up(asciii_to_cmd_1_p2_up),
    .P2_Down(asciii_to_cmd_1_p2_down), .P1_Won(and_1_out), .Clock(clock_1_out),
    .StartUp(startplayer_1_startup), .StartDown(startplayer_1_startdown), .P2_Next(startplayer_1_p2_next));
  BallPos ballpos_1 (
    .StartUp(startplayer_1_startup), .StartDown(startplayer_1_startdown), .ActiveX(counters_1_activex),
    .Enable(and_4_out), .Reset(asciii_to_cmd_1_reset), .ResetPlayer(startplayer_1_p2_next),
    .ReverseX(or_1_out), .ReverseY(or_2_out), .Clock(clock_1_out), .Draw(ballpos_1_draw),
    .PosX(ballpos_1_posx), .PosY(ballpos_1_posy), .PosXNext(ballpos_1_posxnext), .PosYNext(ballpos_1_posynext));
  assign Draw_out = playerpos_1_draw | playerpos_2_draw | ballpos_1_draw;  // OR_Gate Draw, 16 bits wide
  Comparator #(.mode("unsigned"), .width(4)) comparator_1 (
    .a(ballpos_1_posx), .b(4'b0000), .eq(comparator_1_eq));  // open: gt, lt
  Comparator #(.mode("unsigned"), .width(4)) comparator_2 (
    .a(ballpos_1_posx), .b(4'b1111), .eq(comparator_2_eq));  // open: gt, lt
  CollisionCheck collisioncheck_1 (
    .BallPosY(ballpos_1_posy), .BallPosXNext(ballpos_1_posxnext), .BallPosYNext(ballpos_1_posynext),
    .PlayerPosX(4'b0001), .PlayerPosY(playerpos_1_posy), .Collision(collisioncheck_1_collision),
    .Corner(collisioncheck_1_corner));
  CollisionCheck collisioncheck_2 (
    .BallPosY(ballpos_1_posy), .BallPosXNext(ballpos_1_posxnext), .BallPosYNext(ballpos_1_posynext),
    .PlayerPosX(4'b1110), .PlayerPosY(playerpos_2_posy), .Collision(collisioncheck_2_collision),
    .Corner(collisioncheck_2_corner));
  and and_1 (and_1_out, Multiplayer, comparator_2_eq);
  and and_2 (and_2_out, collisioncheck_2_collision, Multiplayer);
  and and_3 (and_3_out, collisioncheck_2_corner, Multiplayer);
  and and_4 (and_4_out, counters_1_logictick, ~comparator_1_eq, ~and_1_out);  // AND_Gate
  or or_1 (or_1_out, collisioncheck_1_collision, and_2_out);
  or or_2 (or_2_out, collisioncheck_1_corner, and_3_out);

  // Notes on the sheet:
  //   Select Keyboard Element to play
  //   New Game: "r"
  //   Player 1: Up: "q" / Down: "a"
  //   Player 2: Up: "o" / Down: "l"
endmodule

module ButtonDebounce (
  input  X,
  input  Clock,
  output Y
);

  wire and_1_out, d_ff_2_q;

  and and_1 (and_1_out, ~d_ff_2_q, X);  // AND_Gate
  D_Flip_Flop d_ff_1 (.D(and_1_out), .clk(Clock), .Q(Y));  // open: Qn, preset, reset
  D_Flip_Flop d_ff_2 (.D(X), .clk(Clock), .Q(d_ff_2_q));  // open: Qn, preset, reset
endmodule

module PlayerPos (
  input  [3:0] ActiveX,
  input  [3:0] PosX,
  input  moveUp,
  input  moveDown,
  input  Reset,
  input  Clock,
  output [15:0] Draw,
  output [15:0] PosY
);

  wire comparator_1_eq;

  Comparator #(.mode("unsigned"), .width(4)) comparator_1 (
    .a(ActiveX), .b(PosX), .eq(comparator_1_eq));  // open: gt, lt
  PlayerPosY playerposy_1 (.Up(moveUp), .Down(moveDown), .Reset(Reset), .Clock(Clock), .Pos(PosY));
  Multiplexer #(.width(16)) multiplexer_1 (.in0({16{1'b0}}), .in1(PosY), .out(Draw), .sel(comparator_1_eq));
endmodule

module PlayerPosY (
  input  Up,
  input  Down,
  input  Reset,
  input  Clock,
  output [15:0] Pos
);

  wire playerposynetz_1_write;
  wire [15:0] multiplexer_1_out, multiplexer_2_out, shifter_1_out, shifter_2_out;

  Shifter #(.shift("lr"), .width(16)) shifter_1 (.in(Pos), .\dist (4'b0001), .out(shifter_1_out));
  Shifter #(.width(16)) shifter_2 (.in(Pos), .\dist (4'b0001), .out(shifter_2_out));
  Multiplexer #(.width(16)) multiplexer_1 (.in0(shifter_1_out), .in1(shifter_2_out), .out(multiplexer_1_out), .sel(Up));
  Multiplexer #(.width(16)) multiplexer_2 (
    .in0(multiplexer_1_out), .in1(16'h380), .out(multiplexer_2_out), .sel(Reset));
  PlayerPosYNetz playerposynetz_1 (
    .Up(Up), .Down(Down), .GOben(Pos[15]), .GUnten(Pos[0]), .Reset(Reset), .Write(playerposynetz_1_write));
  Register #(.width(16)) register_1 (
    .D(multiplexer_2_out), .en(playerposynetz_1_write), .clk(Clock), .Q(Pos));  // open: clr
endmodule

module PlayerPosYNetz (
  input  Up,
  input  Down,
  input  GOben,
  input  GUnten,
  input  Reset,
  output Write
);

  wire and_1_out, and_2_out, not_1_out, not_2_out, not_3_out;

  not not_1 (not_1_out, Up);
  not not_2 (not_2_out, GOben);
  not not_3 (not_3_out, GUnten);
  and and_1 (and_1_out, not_1_out, Down, not_3_out);
  and and_2 (and_2_out, Up, not_2_out);
  or or_1 (Write, Reset, and_1_out, and_2_out);
endmodule

module BallPos (
  input  StartUp,
  input  StartDown,
  input  [3:0] ActiveX,
  input  Enable,
  input  Reset,
  input  ResetPlayer,
  input  ReverseX,
  input  ReverseY,
  input  Clock,
  output [15:0] Draw,
  output [3:0] PosX,
  output [15:0] PosY,
  output [3:0] PosXNext,
  output [15:0] PosYNext
);

  wire comparator_1_eq, comparator_2_eq, comparator_2_gt, or_1_out, or_2_out, or_3_out;
  wire [3:0] multiplexer_1_out;

  or or_1 (or_1_out, StartUp, StartDown);
  or or_2 (or_2_out, ReverseX, or_3_out);
  Multiplexer #(.width(4)) multiplexer_1 (.in0(4'b0010), .in1(4'b1101), .out(multiplexer_1_out), .sel(ResetPlayer));
  BallPosY ballposy_1 (
    .StartUp(StartUp), .StartDown(StartDown), .Reverse(ReverseY), .Reset(Reset), .Enable(Enable),
    .Clock(Clock), .PosYNext(PosYNext), .PosY(PosY));
  BallPosX ballposx_1 (
    .Start(or_1_out), .Reverse(or_2_out), .Enable(Enable), .Reset(Reset), .ResetWert(multiplexer_1_out),
    .Clock(Clock), .PosX(PosX), .PosXNext(PosXNext));
  Multiplexer #(.width(16)) multiplexer_2 (.in0({16{1'b0}}), .in1(PosY), .out(Draw), .sel(comparator_1_eq));
  Comparator #(.mode("unsigned"), .width(4)) comparator_1 (
    .a(ActiveX), .b(PosX), .eq(comparator_1_eq));  // open: gt, lt
  Comparator #(.mode("unsigned"), .width(4)) comparator_2 (
    .a(PosX), .b(4'b1111), .gt(comparator_2_gt), .eq(comparator_2_eq));  // open: lt
  or or_3 (or_3_out, comparator_2_gt, comparator_2_eq);
endmodule

module BallPosX (
  input  Start,
  input  Reverse,
  input  Enable,
  input  Reset,
  input  [3:0] ResetWert,
  input  Clock,
  output [3:0] PosX,
  output [3:0] PosXNext
);

  wire and_1_out, and_2_out, ballposxdirnetz_1_d_new, comparator_1_eq, comparator_2_eq, d_ff_1_q, d_ff_2_q,
       or_1_out, or_2_out;
  wire [3:0] adder_1_out, multiplexer_1_out, subtractor_1_out;

  or or_1 (or_1_out, d_ff_1_q, Start);
  and and_1 (and_1_out, or_1_out, ~Reset);  // AND_Gate
  and and_2 (and_2_out, and_1_out, Enable);
  BallPosXDirNetz ballposxdirnetz_1 (
    .Reverse(Reverse), .Enable(Enable), .Reset(Reset), .D_old(d_ff_2_q), .D_new(ballposxdirnetz_1_d_new));
  D_Flip_Flop d_ff_1 (.D(and_1_out), .clk(Clock), .Q(d_ff_1_q));  // open: Qn, preset, reset
  D_Flip_Flop d_ff_2 (.D(ballposxdirnetz_1_d_new), .clk(Clock), .Q(d_ff_2_q));  // open: Qn, preset, reset
  Counter #(.max('hf), .ongoal("stay"), .width(4)) counter_1 (
    .load(Reset), .up(ballposxdirnetz_1_d_new), .count(and_2_out), .clk(Clock), .D(ResetWert), .Q(PosX));  // open: clr, carry
  Subtractor #(.width(4)) subtractor_1 (.a(PosX), .b(4'b0001), .out(subtractor_1_out));  // open: bin, bout
  Adder #(.width(4)) adder_1 (.a(PosX), .b(4'b0001), .out(adder_1_out));  // open: cin, cout
  Comparator #(.mode("unsigned"), .width(4)) comparator_1 (
    .a(4'b0000), .b(PosX), .eq(comparator_1_eq));  // open: gt, lt
  Comparator #(.mode("unsigned"), .width(4)) comparator_2 (
    .a(PosX), .b(4'b1111), .eq(comparator_2_eq));  // open: gt, lt
  Multiplexer #(.width(4)) multiplexer_1 (
    .in0(subtractor_1_out), .in1(adder_1_out), .out(multiplexer_1_out), .sel(d_ff_2_q));
  Multiplexer #(.width(4)) multiplexer_2 (.in0(multiplexer_1_out), .in1(PosX), .out(PosXNext), .sel(or_2_out));
  or or_2 (or_2_out, comparator_1_eq, comparator_2_eq);

  // Notes on the sheet:
  //   ResetWert: initial=0x2
endmodule

module BallPosXDirNetz (
  input  Reverse,
  input  Enable,
  input  Reset,
  input  D_old,
  output D_new
);

  wire and_1_out, and_2_out, and_3_out, not_1_out, not_2_out, not_3_out;

  not not_1 (not_1_out, Reverse);
  not not_2 (not_2_out, Enable);
  not not_3 (not_3_out, D_old);
  and and_1 (and_1_out, not_1_out, D_old);
  and and_2 (and_2_out, not_2_out, D_old);
  and and_3 (and_3_out, Reverse, Enable, not_3_out);
  or or_1 (D_new, Reset, and_1_out, and_2_out, and_3_out);
endmodule

module BallPosY (
  input  StartUp,
  input  StartDown,
  input  Reverse,
  input  Reset,
  input  Enable,
  input  Clock,
  output [15:0] PosYNext,
  output [15:0] PosY
);

  wire and_1_out, ballposydir_1_down_simple, ballposydir_1_down_true, ballposydir_1_up_simple,
       ballposydir_1_up_true, ballposywritenetz_1_write;
  wire [15:0] ballposyshifter_2_pos_new;

  and and_1 (and_1_out, Reverse, Enable);
  BallPosYDir ballposydir_1 (
    .Pos(PosY), .StartUp(StartUp), .StartDown(StartDown), .Reverse(and_1_out), .Stop(Reset), .Clock(Clock),
    .Up_True(ballposydir_1_up_true), .Down_True(ballposydir_1_down_true),
    .Up_Simple(ballposydir_1_up_simple), .Down_Simple(ballposydir_1_down_simple));
  BallPosYShifter ballposyshifter_1 (
    .Up(ballposydir_1_up_simple), .Down(ballposydir_1_down_simple), .Pos_Old(PosY), .Pos_New(PosYNext));
  BallPosYShifter ballposyshifter_2 (
    .Up(ballposydir_1_up_true), .Down(ballposydir_1_down_true), .Pos_Old(PosY),
    .Pos_New(ballposyshifter_2_pos_new));
  BallPosYWriteNetz ballposywritenetz_1 (
    .Up(ballposydir_1_up_true), .Down(ballposydir_1_down_true), .Enable(Enable), .Reset(Reset),
    .Write(ballposywritenetz_1_write));
  Register #(.width(16)) register_1 (
    .D(ballposyshifter_2_pos_new), .en(ballposywritenetz_1_write), .clk(Clock), .Q(PosY));  // open: clr
endmodule

module BallPosYDir (
  input  [15:0] Pos,
  input  StartUp,
  input  StartDown,
  input  Reverse,
  input  Stop,
  input  Clock,
  output Up_True,
  output Down_True,
  output Up_Simple,
  output Down_Simple
);

  wire d_ff_1_q, d_ff_2_q;

  BallPosYDirNetz ballposydirnetz_1 (
    .Up(d_ff_1_q), .Down(d_ff_2_q), .GOben(Pos[15]), .GUnten(Pos[0]), .StartUp(StartUp),
    .StartDown(StartDown), .Reverse(Reverse), .Stop(Stop), .Up_True(Up_True), .Down_True(Down_True),
    .Up_Simple(Up_Simple), .Down_Simple(Down_Simple));
  D_Flip_Flop d_ff_1 (.D(Up_True), .clk(Clock), .Q(d_ff_1_q));  // open: Qn, preset, reset
  D_Flip_Flop d_ff_2 (.D(Down_True), .clk(Clock), .Q(d_ff_2_q));  // open: Qn, preset, reset
endmodule

module BallPosYDirNetz (
  input  Up,
  input  Down,
  input  GOben,
  input  GUnten,
  input  StartUp,
  input  StartDown,
  input  Reverse,
  input  Stop,
  output Up_True,
  output Down_True,
  output Up_Simple,
  output Down_Simple
);

  wire and_1_out, and_2_out, and_3_out, and_4_out, and_5_out, and_6_out, and_7_out, and_8_out, and_9_out,
       and_10_out, and_11_out, and_12_out, and_13_out, and_14_out, not_1_out, not_2_out, not_3_out,
       not_4_out, not_5_out, not_6_out, not_7_out;

  not not_1 (not_1_out, Up);
  not not_2 (not_2_out, Down);
  not not_3 (not_3_out, GOben);
  not not_4 (not_4_out, GUnten);
  not not_5 (not_5_out, StartUp);
  not not_6 (not_6_out, Reverse);
  not not_7 (not_7_out, Stop);
  and and_1 (and_1_out, Up, not_3_out, not_6_out, not_7_out);
  and and_2 (and_2_out, not_1_out, Down, not_3_out, Reverse, not_7_out);
  and and_3 (and_3_out, not_3_out, GUnten, not_7_out);
  and and_4 (and_4_out, not_1_out, not_2_out, not_3_out, StartUp, not_7_out);
  and and_5 (and_5_out, Up, not_4_out, Reverse, not_7_out);
  and and_6 (and_6_out, GOben, not_7_out);
  and and_7 (and_7_out, not_1_out, Down, not_4_out, not_6_out, not_7_out);
  and and_8 (and_8_out, not_1_out, not_2_out, not_4_out, not_5_out, StartDown, not_7_out);
  and and_9 (and_9_out, Up, not_3_out, not_7_out);
  and and_10 (and_10_out, not_2_out, not_3_out, StartUp, not_7_out);
  and and_11 (and_11_out, not_3_out, GUnten, not_7_out);
  and and_12 (and_12_out, not_1_out, not_4_out, not_5_out, StartDown, not_7_out);
  and and_13 (and_13_out, GOben, not_7_out);
  and and_14 (and_14_out, not_1_out, Down, not_4_out, not_7_out);
  or or_1 (Up_True, and_1_out, and_2_out, and_3_out, and_4_out);
  or or_2 (Down_True, and_5_out, and_6_out, and_7_out, and_8_out);
  or or_3 (Up_Simple, and_9_out, and_10_out, and_11_out);
  or or_4 (Down_Simple, and_12_out, and_13_out, and_14_out);
endmodule

module BallPosYShifter (
  input  Up,
  input  Down,
  input  [15:0] Pos_Old,
  output [15:0] Pos_New
);

  wire or_1_out;
  wire [15:0] multiplexer_1_out, shifter_1_out, shifter_2_out;

  Shifter #(.shift("lr"), .width(16)) shifter_1 (.in(Pos_Old), .\dist (4'b0001), .out(shifter_1_out));
  Multiplexer #(.width(16)) multiplexer_1 (.in0(shifter_1_out), .in1(shifter_2_out), .out(multiplexer_1_out), .sel(Up));
  Shifter #(.width(16)) shifter_2 (.in(Pos_Old), .\dist (4'b0001), .out(shifter_2_out));
  or or_1 (or_1_out, Up, Down);
  Multiplexer #(.width(16)) multiplexer_2 (.in0(16'h100), .in1(multiplexer_1_out), .out(Pos_New), .sel(or_1_out));
endmodule

module BallPosYWriteNetz (
  input  Up,
  input  Down,
  input  Enable,
  input  Reset,
  output Write
);

  wire and_1_out, and_2_out;

  and and_1 (and_1_out, Down, Enable);
  and and_2 (and_2_out, Up, Enable);
  or or_1 (Write, Reset, and_1_out, and_2_out);
endmodule

module Counters (
  input  Clock,
  output LogicTick,
  output [3:0] ActiveX
);

  Counter #(.max('hf), .width(4)) counter_1 (
    .clk(Clock), .carry(LogicTick), .Q(ActiveX));  // open: clr, load, up, count, D
endmodule

module CollisionCheck (
  input  [15:0] BallPosY,
  input  [3:0] BallPosXNext,
  input  [15:0] BallPosYNext,
  input  [3:0] PlayerPosX,
  input  [15:0] PlayerPosY,
  output Collision,
  output Corner
);

  wire comparator_1_eq, comparator_2_gt, comparator_3_eq;
  wire [15:0] and_1_out, and_2_out;

  assign and_1_out = BallPosYNext & PlayerPosY;  // AND_Gate and_1, 16 bits wide
  assign and_2_out = PlayerPosY & BallPosY;  // AND_Gate and_2, 16 bits wide
  Comparator #(.mode("unsigned"), .width(4)) comparator_1 (
    .a(BallPosXNext), .b(PlayerPosX), .eq(comparator_1_eq));  // open: gt, lt
  Comparator #(.mode("unsigned"), .width(16)) comparator_2 (
    .a(and_1_out), .b({16{1'b0}}), .gt(comparator_2_gt));  // open: eq, lt
  Comparator #(.mode("unsigned"), .width(16)) comparator_3 (
    .a(and_2_out), .b({16{1'b0}}), .eq(comparator_3_eq));  // open: gt, lt
  and and_3 (Collision, comparator_1_eq, comparator_2_gt);
  and and_4 (Corner, Collision, comparator_3_eq);
endmodule

module VRAM16 (
  input  [3:0] Addr,
  input  [15:0] Wert,
  input  Clk,
  output [15:0] out_4,
  output [15:0] out_5,
  output [15:0] out_6,
  output [15:0] out_7,
  output [15:0] out_8,
  output [15:0] out_9,
  output [15:0] out_10,
  output [15:0] out_11,
  output [15:0] out_12,
  output [15:0] out_13,
  output [15:0] out_14,
  output [15:0] out_15,
  output [15:0] out_16,
  output [15:0] out_17,
  output [15:0] out_18,
  output [15:0] out_19
);

  wire not_1_out;
  wire [15:0] demultiplexer_1_out0, demultiplexer_1_out1;

  not not_1 (not_1_out, Addr[3]);
  Demultiplexer #(.width(16)) demultiplexer_1 (
    .out0(demultiplexer_1_out0), .out1(demultiplexer_1_out1), .in(Wert), .sel(Addr[3]));
  VRAM8 vram8_1 (
    .Addr(Addr[2:0]), .Wert(demultiplexer_1_out0), .Enable(not_1_out), .Clk(Clk), .out_5(out_4),
    .out_6(out_5), .out_7(out_6), .out_8(out_7), .out_9(out_8), .out_10(out_9), .out_11(out_10),
    .out_12(out_11));
  VRAM8 vram8_2 (
    .Addr(Addr[2:0]), .Wert(demultiplexer_1_out1), .Enable(Addr[3]), .Clk(Clk), .out_5(out_12),
    .out_6(out_13), .out_7(out_14), .out_8(out_15), .out_9(out_16), .out_10(out_17), .out_11(out_18),
    .out_12(out_19));
endmodule

module VRAM8 (
  input  [2:0] Addr,
  input  [15:0] Wert,
  input  Enable,
  input  Clk,
  output [15:0] out_5,
  output [15:0] out_6,
  output [15:0] out_7,
  output [15:0] out_8,
  output [15:0] out_9,
  output [15:0] out_10,
  output [15:0] out_11,
  output [15:0] out_12
);

  wire and_1_out, and_2_out;
  wire [15:0] demultiplexer_1_out0, demultiplexer_1_out1;

  Demultiplexer #(.width(16)) demultiplexer_1 (
    .out0(demultiplexer_1_out0), .out1(demultiplexer_1_out1), .in(Wert), .sel(Addr[2]));
  and and_1 (and_1_out, ~Addr[2], Enable);  // AND_Gate
  and and_2 (and_2_out, Addr[2], Enable);
  VRAM4 vram4_1 (
    .Addr(Addr[1:0]), .Wert(demultiplexer_1_out0), .Enable(and_1_out), .Clk(Clk), .out_5(out_5),
    .out_6(out_6), .out_7(out_7), .out_8(out_8));
  VRAM4 vram4_2 (
    .Addr(Addr[1:0]), .Wert(demultiplexer_1_out1), .Enable(and_2_out), .Clk(Clk), .out_5(out_9),
    .out_6(out_10), .out_7(out_11), .out_8(out_12));
endmodule

module VRAM4 (
  input  [1:0] Addr,
  input  [15:0] Wert,
  input  Enable,
  input  Clk,
  output [15:0] out_5,
  output [15:0] out_6,
  output [15:0] out_7,
  output [15:0] out_8
);

  wire and_1_out, and_2_out;
  wire [15:0] demultiplexer_1_out0, demultiplexer_1_out1;

  Demultiplexer #(.width(16)) demultiplexer_1 (
    .out0(demultiplexer_1_out0), .out1(demultiplexer_1_out1), .in(Wert), .sel(Addr[1]));
  and and_1 (and_1_out, ~Addr[1], Enable);  // AND_Gate
  and and_2 (and_2_out, Addr[1], Enable);
  VRAM2 vram2_1 (
    .Addr(Addr[0]), .Wert(demultiplexer_1_out0), .Enable(and_1_out), .Clk(Clk), .out_5(out_5), .out_6(out_6));
  VRAM2 vram2_2 (
    .Addr(Addr[0]), .Wert(demultiplexer_1_out1), .Enable(and_2_out), .Clk(Clk), .out_5(out_7), .out_6(out_8));
endmodule

module VRAM2 (
  input  Addr,
  input  [15:0] Wert,
  input  Enable,
  input  Clk,
  output [15:0] out_5,
  output [15:0] out_6
);

  wire and_1_out, and_2_out;
  wire [15:0] demultiplexer_1_out0, demultiplexer_1_out1;

  and and_1 (and_1_out, ~Addr, Enable);  // AND_Gate
  Demultiplexer #(.width(16)) demultiplexer_1 (
    .out0(demultiplexer_1_out0), .out1(demultiplexer_1_out1), .in(Wert), .sel(Addr));
  and and_2 (and_2_out, Addr, Enable);
  Register #(.width(16)) register_1 (.D(demultiplexer_1_out0), .en(and_1_out), .clk(Clk), .Q(out_5));  // open: clr
  Register #(.width(16)) register_2 (.D(demultiplexer_1_out1), .en(and_2_out), .clk(Clk), .Q(out_6));  // open: clr
endmodule

module ASCIII_to_Cmd (
  input  [6:0] in_1,
  output Reset,
  output P1_Up,
  output P1_Down,
  output P2_Up,
  output P2_Down
);

  Comparator #(.mode("unsigned"), .width(7)) comparator_1 (.a(7'b1110010), .b(in_1), .eq(Reset));  // open: gt, lt
  Comparator #(.mode("unsigned"), .width(7)) comparator_2 (.a(7'b1110001), .b(in_1), .eq(P1_Up));  // open: gt, lt
  Comparator #(.mode("unsigned"), .width(7)) comparator_3 (.a(7'b1100001), .b(in_1), .eq(P1_Down));  // open: gt, lt
  Comparator #(.mode("unsigned"), .width(7)) comparator_4 (.a(7'b1101111), .b(in_1), .eq(P2_Up));  // open: gt, lt
  Comparator #(.mode("unsigned"), .width(7)) comparator_5 (.a(7'b1101100), .b(in_1), .eq(P2_Down));  // open: gt, lt
endmodule

module StartPlayer (
  input  P1_Up,
  input  P1_Down,
  input  P2_Up,
  input  P2_Down,
  input  P1_Won,
  input  Clock,
  output StartUp,
  output StartDown,
  output P2_Next
);

  wire startplayernetz_1_p2_next;

  StartPlayerNetz startplayernetz_1 (
    .P1_Up(P1_Up), .P1_Down(P1_Down), .P2_Up(P2_Up), .P2_Down(P2_Down), .P1_Won(P1_Won), .P2_Next_(P2_Next),
    .Up(StartUp), .Down(StartDown), .P2_Next(startplayernetz_1_p2_next));
  D_Flip_Flop d_ff_1 (.D(startplayernetz_1_p2_next), .clk(Clock), .Q(P2_Next));  // open: Qn, preset, reset
endmodule

module StartPlayerNetz (
  input  P1_Up,
  input  P1_Down,
  input  P2_Up,
  input  P2_Down,
  input  P1_Won,
  input  P2_Next_,
  output Up,
  output Down,
  output P2_Next
);

  wire and_1_out, and_2_out, and_3_out, and_4_out, and_5_out, not_1_out, not_2_out, not_3_out, not_4_out;

  not not_1 (not_1_out, P1_Up);
  not not_2 (not_2_out, P2_Up);
  not not_3 (not_3_out, P2_Down);
  not not_4 (not_4_out, P2_Next_);
  and and_1 (and_1_out, P2_Up, P2_Next_);
  and and_2 (and_2_out, P1_Up, not_4_out);
  and and_3 (and_3_out, not_2_out, P2_Down, P2_Next_);
  and and_4 (and_4_out, not_1_out, P1_Down, not_4_out);
  and and_5 (and_5_out, not_2_out, not_3_out, P2_Next_);
  or or_1 (Up, and_1_out, and_2_out);
  or or_2 (Down, and_3_out, and_4_out);
  or or_3 (P2_Next, and_5_out, P1_Won);
endmodule
